# Fritzing sketch schematic (saved by Fritzing 0.9.4)

parts:
  D1 = Rectifier Diode [part_number=1N4001 package="300 mil [THT]"]
  R1 = Resistor [tolerance=±5% resistance=10k package=THT]
  Q1 = MOSFET-NCHANNEL [part_number=IRF3710 package=to220v]
  J1 = Camdenboss CTB0158-2 [part_number=CTB0158-2 package=THT]
  J2 = Camdenboss CTB0158-2 [part_number=CTB0158-2 package=THT]
  Part2 = ACS712 Low Current Sensor Board v12
  J3 = Power Jack [package=power_jack_smd]
  Z1 = VARISTOR [package=0603-res]
  T1 = LM35 Temperature Sensor [package="TO92 [THT]"]
  Part3 = Bluetooth HC-05 Macho
  R2 = Resistor [tolerance=±5% resistance=1k package="0805 [SMD]"]
  R3 = Resistor [tolerance=±5% resistance=2k package="0805 [SMD]"]
  D2 = Rectifier Diode [part_number=1N4001 package="300 mil [THT]"]
  Q2 = MOSFET-NCHANNEL [part_number=IRF3710 package=to220v]
  R4 = Resistor [tolerance=±5% resistance=10k package=THT]
  J4 = Camdenboss CTB0158-2 [part_number=CTB0158-2 package=THT]
  Z2 = VARISTOR [package=0603-res]
  T2 = LM35 Temperature Sensor [package="TO92 [THT]"]
  D3 = Rectifier Diode [part_number=1N4001 package="300 mil [THT]"]
  Q3 = MOSFET-NCHANNEL [part_number=IRF3710 package=to220v]
  R5 = Resistor [tolerance=±5% resistance=10k package=THT]
  J5 = Camdenboss CTB0158-2 [part_number=CTB0158-2 package=THT]
  Z3 = VARISTOR [package=0603-res]
  T3 = LM35 Temperature Sensor [package="TO92 [THT]"]
  Z4 = VARISTOR [package=0603-res]
  Part1 = Arduino Nano (Rev3.0)

nets:
  N1: D1.cathode, Q1.D, J1.pin2
  N2: D1.anode, J1.pin1, Part2.IP+, D2.anode, J4.pin1, D3.anode, J5.pin1, Part1.VIN
  GND: R1.Pin_0, Q1.S, J2.pin1, J3.GNDBREAK, T1.GND, Part3.GND, R3.Pin_1, Q2.S, R4.Pin_0, T2.GND, Q3.S, R5.Pin_0, T3.GND, Part1.GND
  N3: R1.Pin_1, Q1.G, Part1.D5
  N4: J1.terminal_1, Z1.1
  N5: J1.terminal_2, Z1.2
  N6: J2.pin2, Part2.IP-, J3.GND
  5V: Part2.5V, T1.+Vs, Part3.VCC, T2.+Vs, T3.+Vs, Part1.5V
  N7: Part2.VO, Part1.A0
  N8: T1.Vout, Part1.A1
  N9: Part3.State, Part1.D4
  N10: Part3.TXD, Part1.D2
  N11: Part3.RXD, R2.Pin_0, R3.Pin_0
  N12: R2.Pin_1, Part1.D3
  N13: D2.cathode, Q2.D, J4.pin2
  N14: Q2.G, R4.Pin_1, Part1.D6
  N15: J4.terminal_1, Z2.1
  N16: J4.terminal_2, Z2.2
  N17: T2.Vout, Part1.A2
  N18: D3.cathode, Q3.D, J5.pin2
  N19: Q3.G, R5.Pin_1, Part1.D7
  N20: J5.terminal_1, Z3.1, Z4.1
  N21: J5.terminal_2, Z3.2, Z4.2
  N22: T3.Vout, Part1.A3
